# Fritzing sketch audio-detector (saved by Fritzing 0.9.4)
breadboards: 1

parts:
  Part1 = Arduino Nano (Rev3.0) (ICSP)
  LED1 = LED - 5mm [color="Orange (620nm)" package="5 mm [THT]"]
  R1 = Resistor [tolerance=±5% resistance=470 package="0603 [SMD]"]
  IR1 = TSOP312.., 314.. [package=THT]
  LED3 = smd LED [color="Infrared (940nm)" package="0805 [SMD]"]
  S3 = Momentary Switch [package=ksa_sealed_tac_switch]
  S4 = Momentary Switch [package=ksa_sealed_tac_switch]
  LED4 = LED - 5mm [color="Green (570nm)" package="5 mm [THT]"]
  LED5 = LED - 5mm [color="Yellow (595nm)" package="5 mm [THT]"]
  LED6 = LED - 5mm [color="Blue (525nm)" package="5 mm [THT]"]
  R4 = Resistor [tolerance=±5% resistance=470 package="0603 [SMD]"]
  R5 = Resistor [tolerance=±5% resistance=470 package="0603 [SMD]"]
  R6 = Resistor [tolerance=±5% resistance=470 package="0603 [SMD]"]
  R7 = Resistor [tolerance=±5% resistance=470 package="0603 [SMD]"]
  S2 = Pushbutton [package="[SMD]"]
  U1 = TLP621 [package=THT]
  U2 = 3.5mm Audio Jack [package=audio-jack-3.5mm-smd]

nets:
  GND: Part1.GND, Part1.D12/MISO, R1.Pin_0, IR1.GND, S3.4, S4.2, S4.4, R4.Pin_0, R5.Pin_0, R6.Pin_0, R7.Pin_1, S2.Pin_1, S2.Pin_2, S2.Pin_3, S2.Pin_4
  N1: Part1.D2, IR1.Data
  N2: Part1.D3, LED3.anode, U1.Pin_1
  N3: Part1.D6, LED4.anode
  N4: Part1.D7, S4.3
  N5: Part1.D8, S3.3
  N6: Part1.D9, LED5.anode
  N7: Part1.D10, LED6.anode
  N8: Part1.5V, IR1.Vs
  N9: Part1.D13/SCK, LED1.anode
  N10: LED1.cathode, R1.Pin_1
  N11: LED3.cathode, R7.Pin_0, U1.Pin_2
  N12: LED4.cathode, R4.Pin_1
  N13: LED5.cathode, R5.Pin_1
  N14: LED6.cathode, R6.Pin_1
  N15: U1.Pin_4, U2.RIGHT
  N16: U1.Pin_3, U2.SLEEVE

notes:
  IR receiver, HW-447
  connected to D2
  LEDS:
  IR - sends the IR code, connected to PWM D3
  ORANGE - status, connected to D4
  GREEN - audio enabled, connected to D6
  YELLOW - IR code recording, connected to D9
  BLUE - IR code recorded, connected to D10
  Buttons (left to right):
  Button 1 - initiates IRcode recording, connected to D12
  Button 2 - simulates audio signal, connected to D8
  Button 3 - simulates audio 12V trigger, connected to D7
  3.5mm Audio Jack - used as input to amplifier IR receiver
  It is controlled by the optocoupler and D3
